// Logisim project wikiarduino.circ as structural Verilog: 1 circuit, main circuit main
module main (
  input  _9,
  input  _8,
  input  _7,
  input  _6,
  input  _5,
  input  _4,
  input  _3,
  input  _2
);

  LED led_1 (.in(_7));
  LED led_2 (.in(_6));
  LED led_3 (.in(_9));
  LED led_4 (.in(_8));
  LED led_5 (.in(_5));
  LED led_6 (.in(_2));
  LED led_7 (.in(_3));
  LED led_8 (.in(_4));

  // Notes on the sheet:
  //   il numero sotto il pin è il numero del pin sulla board di arduino
endmodule
